// Logisim project CodificadorPrioridade4x2.circ as structural Verilog: 1 circuit, main circuit main
module main (
  input  [3:0] _3_2_1_0,
  output [1:0] _1_0,
  output Eo
);

  wire and_1_out, not_1_out;

  not not_1 (not_1_out, _3_2_1_0[2]);
  and and_1 (and_1_out, not_1_out, _3_2_1_0[1]);
  or or_1 (_1_0[1], _3_2_1_0[2], _3_2_1_0[3]);
  or or_2 (_1_0[0], and_1_out, _3_2_1_0[3]);
  or or_3 (Eo, _3_2_1_0[0], _3_2_1_0[1], _3_2_1_0[2], _3_2_1_0[3]);

  // Notes on the sheet:
  //   Codificador c/ Prioridade e Enable Output 4x2
endmodule
