// Logisim project CodificadorSimples.circ as structural Verilog: 1 circuit, main circuit main
module main (
  input  [3:0] _3_2_1_0,
  output [1:0] out_2
);

  or or_1 (out_2[1], _3_2_1_0[2], _3_2_1_0[3]);
  or or_2 (out_2[0], _3_2_1_0[1], _3_2_1_0[3]);

  // Notes on the sheet:
  //   Codificador Simples
endmodule
