// Logisim project ComparadorDeMagnitude3Bist.circ as structural Verilog: 1 circuit, main circuit main
module main (
  input  [2:0] A,
  input  [2:0] B,
  output out_3,
  output out_4,
  output out_5,
  output out_6
);

  wire not_1_out, not_2_out, not_3_out;

  not not_1 (not_1_out, B[0]);
  not not_2 (not_2_out, B[1]);
  not not_3 (not_3_out, B[2]);
  and and_1 (out_3, A[0], not_1_out);
  and and_2 (out_4, A[1], not_2_out);
  and and_3 (out_6, A[2], not_3_out);
  or or_1 (out_5, out_3, out_4, out_6);

  // Notes on the sheet:
  //   Circuito Comparador Completo de 3 Bits
endmodule
