// Logisim project DecodMuxParaDisplay.circ as structural Verilog: 1 circuit, main circuit main
module main (
  input  Seletor,
  input  [3:0] A,
  input  [3:0] B,
  output [3:0] out_4
);

  wire A_2_out, A_3_out, A_4_out, A_5_out, A_out, and_1_out, and_2_out, and_3_out, and_4_out, and_5_out,
       and_6_out, and_7_out, and_8_out, and_9_out, B_2_out, B_3_out, B_4_out, B_5_out, B_out, C_out, D_out,
       E_out, F_out, G_out, not_1_out, not_2_out, not_3_out, not_4_out, not_5_out, not_6_out, not_7_out,
       not_8_out, not_9_out, not_10_out, not_11_out, not_12_out, not_13_out, not_14_out, not_15_out,
       not_16_out, not_17_out, not_18_out, not_19_out, not_20_out, or_1_out, or_2_out, or_3_out, xnor_1_out,
       xnor_2_out, xor_1_out;

  _7_Segment_Display u_7_segment_display_1 (
    .g(A_5_out), .f(B_5_out), .a(C_out), .b(D_out), .e(E_out), .d(F_out), .c(G_out));  // open: dp
  not not_1 (not_1_out, Seletor);
  not not_2 (not_2_out, Seletor);
  not not_3 (not_3_out, Seletor);
  not not_4 (not_4_out, Seletor);
  and u_A (A_out, A[3], Seletor);
  or _3 (out_4[3], A_out, B_out);
  and u_B (B_out, B[3], not_1_out);
  and A_2 (A_2_out, A[2], Seletor);
  or _2 (out_4[2], A_2_out, B_2_out);
  and B_2 (B_2_out, B[2], not_2_out);
  and A_3 (A_3_out, A[1], Seletor);
  or _1 (out_4[1], A_3_out, B_3_out);
  and B_3 (B_3_out, B[1], not_3_out);
  and A_4 (A_4_out, A[0], Seletor);
  or _0 (out_4[0], A_4_out, B_4_out);
  and B_4 (B_4_out, B[0], not_4_out);
  not not_5 (not_5_out, out_4[0]);
  not not_6 (not_6_out, out_4[1]);
  not not_7 (not_7_out, out_4[0]);
  not not_8 (not_8_out, out_4[1]);
  not not_9 (not_9_out, out_4[0]);
  not not_10 (not_10_out, out_4[2]);
  not not_11 (not_11_out, out_4[2]);
  not not_12 (not_12_out, out_4[2]);
  not not_13 (not_13_out, out_4[3]);
  not not_14 (not_14_out, out_4[0]);
  not not_15 (not_15_out, out_4[1]);
  not not_16 (not_16_out, out_4[2]);
  not not_17 (not_17_out, out_4[0]);
  not not_18 (not_18_out, out_4[1]);
  not not_19 (not_19_out, out_4[3]);
  and and_1 (and_1_out, out_4[2], not_5_out);
  xor xor_1 (xor_1_out, out_4[1], out_4[2]);
  and and_2 (and_2_out, out_4[2], or_1_out);
  or or_1 (or_1_out, not_6_out, not_7_out);
  and and_3 (and_3_out, not_8_out, not_9_out);
  xnor xnor_1 (xnor_1_out, out_4[0], out_4[2]);
  xnor xnor_2 (xnor_2_out, out_4[0], out_4[1]);
  or or_2 (or_2_out, not_11_out, out_4[1]);
  and and_4 (and_4_out, not_12_out, not_13_out);
  or or_3 (or_3_out, and_4_out, out_4[1]);
  and and_5 (and_5_out, out_4[0], not_15_out, out_4[2]);
  and and_6 (and_6_out, out_4[1], not_16_out);
  and and_7 (and_7_out, not_17_out, not_18_out);
  and and_8 (and_8_out, not_19_out, out_4[0]);
  or A_5 (A_5_out, out_4[3], and_1_out, xor_1_out);
  or B_5 (B_5_out, and_2_out, and_3_out, out_4[3]);
  or C (C_out, out_4[3], out_4[1], xnor_1_out);
  or D (D_out, not_10_out, out_4[3], xnor_2_out);
  not not_20 (not_20_out, out_4[0]);
  and and_9 (and_9_out, or_3_out, not_14_out);
  and E (E_out, or_2_out, not_20_out);
  or F (F_out, and_9_out, and_5_out, and_6_out, out_4[3]);
  or G (G_out, and_7_out, and_8_out, out_4[2], out_4[3]);

  // Notes on the sheet:
  //   Decodificador + Multiplexador para Display
endmodule
