// Logisim project Decodificador2x4.circ as structural Verilog: 1 circuit, main circuit main
module main (
  input  [1:0] _1_0,
  output [3:0] _3_2_1_0
);

  wire not_1_out, not_2_out, not_3_out, not_4_out;

  not not_1 (not_1_out, _1_0[0]);
  not not_2 (not_2_out, _1_0[1]);
  not not_3 (not_3_out, _1_0[1]);
  not not_4 (not_4_out, _1_0[0]);
  and and_1 (_3_2_1_0[3], _1_0[0], _1_0[1]);
  and and_2 (_3_2_1_0[2], _1_0[1], not_1_out);
  and and_3 (_3_2_1_0[1], not_2_out, _1_0[0]);
  and and_4 (_3_2_1_0[0], not_3_out, not_4_out);

  // Notes on the sheet:
  //   Decodificador 2x4
endmodule
