// Logisim project Mux2x1.circ as structural Verilog: 1 circuit, main circuit main
module main (
  input  S,
  input  A,
  input  B,
  output out_4,
  output out_5
);

  wire not_1_out;

  and and_1 (out_4, A, S);
  and and_2 (out_5, B, not_1_out);
  not not_1 (not_1_out, S);

  // Notes on the sheet:
  //   Multiplexador 2x1
endmodule
