// Logisim project Flip_Flop_D.circ as structural Verilog: 5 circuits, main circuit Flip Flop D
module Flip_Flop_D (
  input  in_1,
  input  in_2,
  output out_3,
  output out_4
);

  wire not_1_out;

  not not_1 (not_1_out, in_1);
  Flip_Flop_SR flip_flop_sr_1 (.S(in_1), .out_4(out_3), .out_5(out_4), .En(in_2), .S_2(not_1_out));
endmodule

module Flip_Flop_SR (
  input  S,
  input  En,
  input  S_2,
  output out_4,
  output out_5
);

  wire detector_de_borda_1_out_2;

  Detector_de_Borda detector_de_borda_1 (.En(En), .out_2(detector_de_borda_1_out_2));
  Latch_SR_Controlado latch_sr_controlado_1 (
    .S(S), .En(detector_de_borda_1_out_2), .R(S_2), .out_4(out_4), .out_5(out_5));
endmodule

module Detector_de_Borda (
  input  En,
  output out_2
);

  wire and_2_out, not_1_out;

  and and_1 (out_2, En, not_1_out);
  not not_1 (not_1_out, and_2_out);
  and and_2 (and_2_out, En, En);
endmodule

module Latch_SR_Controlado (
  input  S,
  input  En,
  input  R,
  output out_4,
  output out_5
);

  wire nand_1_out, nand_2_out;

  nand nand_1 (nand_1_out, S, En);
  nand nand_2 (nand_2_out, En, R);
  Latch_SR__Nand latch_sr_nand_1 (.Q_prime(out_5), .Q(out_4), .S(nand_1_out), .R(nand_2_out));
endmodule

module Latch_SR__Nand (
  input  S,
  input  R,
  output Q,
  output Q_prime
);

  nand nand_1 (Q, S, Q_prime);
  nand nand_2 (Q_prime, Q, R);
endmodule
