// Logisim project Latch_SR (Nand).circ as structural Verilog: 1 circuit, main circuit main
module main (
  input  S,
  input  R,
  input  S_2,
  input  R_2,
  output Q,
  output Q_prime,
  output Q_2,
  output Q_prime_2
);

  wire not_1_out, not_2_out;

  not not_1 (not_1_out, S);
  not not_2 (not_2_out, R);
  nand nand_1 (Q, not_1_out, Q_prime);
  nand nand_2 (Q_prime, Q, not_2_out);
  nand nand_3 (Q_2, S_2, Q_prime_2);
  nand nand_4 (Q_prime_2, Q_2, R_2);
endmodule
