// Logisim project Latch_SR_Controlado_(Nor).circ as structural Verilog: 2 circuits, main circuit Latch SR Controlado (Nor)
module Latch_SR_Controlado__Nor (
  input  R,
  input  En,
  input  S,
  output out_4,
  output out_5
);

  wire and_1_out, and_2_out;

  and and_1 (and_1_out, R, En);
  and and_2 (and_2_out, En, S);
  Latch_SR__Nor latch_sr_nor_1 (.Q_prime(out_5), .Q(out_4), .R(and_1_out), .S(and_2_out));
endmodule

module Latch_SR__Nor (
  input  R,
  input  S,
  output Q,
  output Q_prime
);

  nor nor_1 (Q, R, Q_prime);
  nor nor_2 (Q_prime, Q, S);
endmodule
