// Logisim project Latch_Tipo_D (Nand).circ as structural Verilog: 2 circuits, main circuit Latch Tipo D (Nand)
module Latch_Tipo_D__Nand (
  input  D,
  input  En,
  output out_3,
  output out_4
);

  wire nand_1_out, nand_2_out, not_1_out;

  not not_1 (not_1_out, D);
  nand nand_1 (nand_1_out, D, En);
  nand nand_2 (nand_2_out, En, not_1_out);
  Latch_SR__Nand latch_sr_nand_1 (.Q_prime(out_4), .Q(out_3), .S(nand_1_out), .R(nand_2_out));
endmodule

module Latch_SR__Nand (
  input  S,
  input  R,
  output Q,
  output Q_prime
);

  nand nand_1 (Q, S, Q_prime);
  nand nand_2 (Q_prime, Q, R);
endmodule
