// Logisim project Latch_Tipo_D (Nor).circ as structural Verilog: 2 circuits, main circuit Latch Tipo D (Nor)
module Latch_Tipo_D__Nor (
  input  D,
  input  En,
  output out_3,
  output out_4
);

  wire nand_1_out, nand_2_out, not_1_out;

  nand nand_1 (nand_1_out, D, En);
  nand nand_2 (nand_2_out, En, not_1_out);
  not not_1 (not_1_out, D);
  Latch_SR__Nor latch_sr_nor_1 (.Q_prime(out_4), .Q(out_3), .R(nand_1_out), .S(nand_2_out));
endmodule

module Latch_SR__Nor (
  input  R,
  input  S,
  output Q,
  output Q_prime
);

  nor nor_1 (Q, R, Q_prime);
  nor nor_2 (Q_prime, Q, S);
endmodule
