// Logisim project Flip_Flop_JK.circ as structural Verilog: 6 circuits, main circuit Flip Flop JK
module Main (
  input  Preset_Async,
  input  J,
  input  K,
  input  Clear_Async,
  output Q,
  output Q_prime
);

  wire clock_1_out;

  Flip_Flop_JK flip_flop_jk_1 (
    .J(J), .K(K), .out_6(Q), .out_7(Q_prime), .Preset(Preset_Async), .Clear(Clear_Async), .CLK(clock_1_out));
  Clock clock_1 (.out(clock_1_out));
endmodule

module Flip_Flop_JK (
  input  Preset,
  input  J,
  input  CLK,
  input  K,
  input  Clear,
  output out_6,
  output out_7
);

  wire and_1_out, and_2_out;

  and and_1 (and_1_out, out_7, J);
  and and_2 (and_2_out, K, out_6);
  Flip_Flop_SR flip_flop_sr_1 (
    .S(and_1_out), .R(and_2_out), .out_6(out_6), .out_7(out_7), .En(CLK), .Preset(Preset), .Clear(Clear));
endmodule

module Flip_Flop_SR (
  input  Preset,
  input  S,
  input  En,
  input  R,
  input  Clear,
  output out_6,
  output out_7
);

  wire detector_de_borda_1_out_2;

  Detector_de_Borda detector_de_borda_1 (.En(En), .out_2(detector_de_borda_1_out_2));
  Latch_SR_Controlado latch_sr_controlado_1 (
    .S(S), .En(detector_de_borda_1_out_2), .R(R), .out_6(out_6), .out_7(out_7), .Preset(Preset), .Clear(Clear));
endmodule

module Detector_de_Borda (
  input  En,
  output out_2
);

  wire and_1_out, not_1_out;

  and and_1 (and_1_out, En, En);
  and and_2 (out_2, En, not_1_out);
  not not_1 (not_1_out, and_1_out);
endmodule

module Latch_SR_Controlado (
  input  Preset,
  input  S,
  input  En,
  input  R,
  input  Clear,
  output out_6,
  output out_7
);

  wire nand_1_out, nand_2_out;

  nand nand_1 (nand_1_out, S, En);
  nand nand_2 (nand_2_out, En, R);
  Latch_SR__Nand latch_sr_nand_1 (
    .Q_prime(out_7), .Q(out_6), .S(nand_1_out), .R(nand_2_out), .Clear(Clear), .Preset(Preset));
endmodule

module Latch_SR__Nand (
  input  Preset,
  input  S,
  input  R,
  input  Clear,
  output Q,
  output Q_prime
);

  nand nand_1 (Q, ~Preset, S, Q_prime);  // NAND_Gate
  nand nand_2 (Q_prime, Q, R, ~Clear);  // NAND_Gate
endmodule
