// Logisim project 10Mhz.circ as structural Verilog: 9 circuits, main circuit Contador
module Main (
  input  in_1
);

  wire clock_1_out;
  wire [3:0] contador_1_p3;

  Clock clock_1 (.out(clock_1_out));
  // Contador contador_1: pin names not known; wires that end beside it: clock_1_out, in_1, contador_1_p3
  Hex_Digit_Display hex_digit_display_1 (.value(contador_1_p3));  // open: dp
endmodule

module Contador (
  input  Preset_Async,
  input  Inicio,
  input  in_3,
  input  in_4,
  output [3:0] out_5,
  output out_6,
  output out_7
);

  wire and_1_out, and_3_out, clock_1_out, flip_flop_t_5_q_prime, not_1_out, not_2_out, or_1_out;

  Clock clock_1 (.out(clock_1_out));
  Flip_Flop_T flip_flop_t_1 (
    .T(1'b1), .Q(out_5[0]), .Preset_Async(Preset_Async), .Clear_Async(or_1_out), .CLK(not_1_out),
    .Clear_Sync(or_1_out));  // open: Q_prime
  not not_1 (not_1_out, clock_1_out);
  or or_1 (or_1_out, Inicio, out_7);
  Flip_Flop_T flip_flop_t_2 (
    .T(out_5[0]), .Q(out_5[1]), .Preset_Async(Preset_Async), .Clear_Async(or_1_out), .CLK(not_1_out),
    .Clear_Sync(or_1_out));  // open: Q_prime
  and and_1 (and_1_out, out_5[0], out_5[1]);
  and and_2 (out_7, out_5[1], not_2_out);
  Flip_Flop_T flip_flop_t_3 (
    .T(and_1_out), .Q(out_5[2]), .Preset_Async(Preset_Async), .Clear_Async(or_1_out), .CLK(not_1_out),
    .Clear_Sync(or_1_out));  // open: Q_prime
  Flip_Flop_T flip_flop_t_4 (
    .T(1'b1), .Q(out_6), .Preset_Async(in_3), .Clear_Async(in_4), .CLK(out_7), .Clear_Sync(in_4));  // open: Q_prime
  and and_3 (and_3_out, and_1_out, out_5[2]);
  Flip_Flop_T flip_flop_t_5 (
    .T(and_3_out), .Q(out_5[3]), .Q_prime(flip_flop_t_5_q_prime), .Preset_Async(Preset_Async),
    .Clear_Async(or_1_out), .CLK(not_1_out), .Clear_Sync(or_1_out));
  Hex_Digit_Display hex_digit_display_1 (.value(out_5));  // open: dp
  not not_2 (not_2_out, flip_flop_t_5_q_prime);
endmodule

module Flip_Flop_T (
  input  Preset_Async,
  input  T,
  input  CLK,
  input  Clear_Sync,
  input  Clear_Async,
  output Q,
  output Q_prime
);

  Flip_Flop_JK flip_flop_jk_1 (
    .J(T), .K(T), .out_7(Q), .out_8(Q_prime), .Preset(Preset_Async), .Clear_Async(Clear_Async), .CLK(CLK),
    .Clear_Sync(Clear_Sync));
endmodule

module Flip_Flop_JK (
  input  Preset,
  input  J,
  input  CLK,
  input  K,
  input  Clear_Sync,
  input  Clear_Async,
  output out_7,
  output out_8
);

  wire and_1_out, and_2_out;

  and and_1 (and_1_out, out_8, J);
  and and_2 (and_2_out, K, out_7);
  Flip_Flop_SR flip_flop_sr_1 (
    .S(and_1_out), .R(and_2_out), .out_7(out_7), .out_8(out_8), .En(CLK), .Preset(Preset),
    .Clear_Async(Clear_Async), .Clear_Sync(Clear_Sync));
endmodule

module Flip_Flop_SR (
  input  Preset,
  input  S,
  input  En,
  input  R,
  input  Clear_Sync,
  input  Clear_Async,
  output out_7,
  output out_8
);

  wire and_1_out, detector_de_borda_descida_1_out_2, or_1_out;

  Detector_de_Borda_Descida detector_de_borda_descida_1 (.En(En), .out_2(detector_de_borda_descida_1_out_2));
  and and_1 (and_1_out, detector_de_borda_descida_1_out_2, Clear_Sync);
  or or_1 (or_1_out, and_1_out, Clear_Async);
  Latch_SR_Controlado latch_sr_controlado_1 (
    .S(S), .En(detector_de_borda_descida_1_out_2), .R(R), .out_6(out_7), .out_7(out_8), .Preset(Preset),
    .Clear(or_1_out));
endmodule

module Detector_de_Borda_Descida (
  input  En,
  output out_2
);

  wire and_1_out, not_1_out, not_2_out;

  not not_1 (not_1_out, En);
  and and_1 (and_1_out, not_1_out, not_1_out);
  and and_2 (out_2, not_1_out, not_2_out);
  not not_2 (not_2_out, and_1_out);
endmodule

module Latch_SR_Controlado (
  input  Preset,
  input  S,
  input  En,
  input  R,
  input  Clear,
  output out_6,
  output out_7
);

  wire nand_1_out, nand_2_out;

  nand nand_1 (nand_1_out, S, En);
  nand nand_2 (nand_2_out, En, R);
  Latch_SR__Nand latch_sr_nand_1 (
    .Q_prime(out_7), .Q(out_6), .S(nand_1_out), .R(nand_2_out), .Clear(Clear), .Preset(Preset));
endmodule

module Latch_SR__Nand (
  input  Preset,
  input  S,
  input  R,
  input  Clear,
  output Q,
  output Q_prime
);

  nand nand_1 (Q, ~Preset, S, Q_prime);  // NAND_Gate
  nand nand_2 (Q_prime, Q, R, ~Clear);  // NAND_Gate
endmodule

module Teste (
  input  in_1,
  input  in_2,
  input  in_3,
  input  in_4,
  output out_5
);

  // Flip_Flop_T flip_flop_t_1: pin names not known; wires that end beside it: in_2, in_3, in_1, in_4, out_5
endmodule
