// Logisim project Registrador_4_Bits.circ as structural Verilog: 3 circuits, main circuit Registrador 4 Bits
module Registrador_4_Bits (
  input  D3,
  input  D2,
  input  D1,
  input  D0,
  input  En,
  output Q3,
  output Q2,
  output Q1,
  output Q0,
  output [3:0] out_10
);

  Latch_Tipo_D latch_tipo_d_1 (.D(D3), .out_3(out_10[3]), .En(En));  // open: out_4
  Latch_Tipo_D latch_tipo_d_2 (.D(D2), .out_3(out_10[2]), .En(En));  // open: out_4
  Latch_Tipo_D latch_tipo_d_3 (.D(D1), .out_3(out_10[1]), .En(En));  // open: out_4
  Latch_Tipo_D latch_tipo_d_4 (.D(D0), .out_3(out_10[0]), .En(En));  // open: out_4
  Hex_Digit_Display hex_digit_display_1 (.value(out_10));  // open: dp

  assign Q0 = out_10[0];
  assign Q1 = out_10[1];
  assign Q2 = out_10[2];
  assign Q3 = out_10[3];
endmodule

module Latch_Tipo_D (
  input  D,
  input  En,
  output out_3,
  output out_4
);

  wire nand_1_out, nand_2_out, not_1_out;

  not not_1 (not_1_out, D);
  nand nand_1 (nand_1_out, D, En);
  nand nand_2 (nand_2_out, En, not_1_out);
  Latch_SR__Nand latch_sr_nand_1 (.Q_prime(out_4), .Q(out_3), .S(nand_1_out), .R(nand_2_out));
endmodule

module Latch_SR__Nand (
  input  S,
  input  R,
  output Q,
  output Q_prime
);

  nand nand_1 (Q, S, Q_prime);
  nand nand_2 (Q_prime, Q, R);
endmodule
