// Logisim project SomadorCompletoUmBit.circ as structural Verilog: 1 circuit, main circuit main
module main (
  input  A,
  input  B,
  input  Ci,
  output Carry_Out,
  output Soma
);

  wire AND_2_out, AND_3_out, AND_out, XOR_out;

  and AND (AND_out, A, B);
  and AND_2 (AND_2_out, A, Ci);
  and AND_3 (AND_3_out, B, Ci);
  xor XOR (XOR_out, A, B);
  or OR (Carry_Out, AND_out, AND_2_out, AND_3_out);
  xor XOR_2 (Soma, XOR_out, Ci);

  // Notes on the sheet:
  //   Circuito somador Completo - 1 bit
endmodule
