// Logisim project SomadorCompleto.circ as structural Verilog: 7 circuits, main circuit main
module main (
  input  [3:0] in_1,
  input  [3:0] in_2
);

  wire somador_de_4_bits_1_carry_out;
  wire [3:0] somador_de_4_bits_1_saida;

  Somador_De_4_Bits somador_de_4_bits_1 (
    .B(in_2), .A(in_1), .Saida(somador_de_4_bits_1_saida), .Carry_Out(somador_de_4_bits_1_carry_out));  // open: in_2
endmodule

module Meio_Somador (
  input  A0,
  input  B0,
  output Soma,
  output Carry_Out
);

  xor xor_1 (Soma, A0, B0);
  and and_1 (Carry_Out, A0, B0);
endmodule

module Somador_Completo__Abstraido (
  input  A,
  input  B,
  input  Ci,
  output Soma,
  output Co
);

  wire meio_somador_1_carry_out, meio_somador_1_soma, meio_somador_2_carry_out;

  Meio_Somador meio_somador_1 (.Soma(meio_somador_1_soma), .Carry_Out(meio_somador_1_carry_out), .A0(A), .B0(B));
  Meio_Somador meio_somador_2 (.Soma(Soma), .Carry_Out(meio_somador_2_carry_out), .A0(meio_somador_1_soma), .B0(Ci));
  or or_1 (Co, meio_somador_2_carry_out, meio_somador_1_carry_out);
endmodule

module Somador_Completo (
  input  Ci,
  input  A,
  input  B,
  input  B_Inverte,
  output Carry_Out,
  output Soma
);

  wire and_1_out, and_2_out, mux_1_bit_1_s_2, xor_1_out;

  Mux_1_Bit mux_1_bit_1 (.X(B), .S(B_Inverte), .S_2(mux_1_bit_1_s_2));
  xor xor_1 (xor_1_out, A, mux_1_bit_1_s_2);
  and and_1 (and_1_out, A, mux_1_bit_1_s_2);
  xor xor_2 (Soma, Ci, xor_1_out);
  and and_2 (and_2_out, Ci, xor_1_out);
  or or_1 (Carry_Out, and_1_out, and_2_out);
endmodule

module Somador_De_4_Bits (
  input  [3:0] A,
  input  in_2,
  input  [3:0] B,
  output [3:0] Saida,
  output Carry_Out
);

  wire somador_completo_1_carry_out, somador_completo_2_carry_out, somador_completo_3_carry_out;

  Somador_Completo somador_completo_1 (
    .Carry_Out(somador_completo_1_carry_out), .Soma(Saida[0]), .Ci(in_2), .A(A[0]), .B(B[0]), .B_Inverte(in_2));
  Somador_Completo somador_completo_2 (
    .Carry_Out(somador_completo_2_carry_out), .Soma(Saida[1]), .Ci(somador_completo_1_carry_out), .A(A[1]),
    .B(B[1]), .B_Inverte(in_2));
  Somador_Completo somador_completo_3 (
    .Carry_Out(somador_completo_3_carry_out), .Soma(Saida[2]), .Ci(somador_completo_2_carry_out), .A(A[2]),
    .B(B[2]), .B_Inverte(in_2));
  Somador_Completo somador_completo_4 (
    .Carry_Out(Carry_Out), .Soma(Saida[3]), .Ci(somador_completo_3_carry_out), .A(A[3]), .B(B[3]),
    .B_Inverte(in_2));
endmodule

module Somador_Completo__Overflow (
  input  [3:0] A,
  input  [3:0] B,
  output [3:0] Saida,
  output Overflow,
  output Overflow_2,
  output Carry_Out
);

  wire and_1_out, and_2_out, somador_completo_abstraido_1_co, somador_completo_abstraido_2_co,
       somador_completo_abstraido_3_co;

  Somador_Completo__Abstraido somador_completo_abstraido_1 (
    .A(B[0]), .B(A[0]), .Ci(1'b0), .Soma(Saida[0]), .Co(somador_completo_abstraido_1_co));
  Somador_Completo__Abstraido somador_completo_abstraido_2 (
    .A(B[1]), .B(A[1]), .Ci(somador_completo_abstraido_1_co), .Soma(Saida[1]),
    .Co(somador_completo_abstraido_2_co));
  Somador_Completo__Abstraido somador_completo_abstraido_3 (
    .A(B[2]), .B(A[2]), .Ci(somador_completo_abstraido_2_co), .Soma(Saida[2]),
    .Co(somador_completo_abstraido_3_co));
  Somador_Completo__Abstraido somador_completo_abstraido_4 (
    .A(B[3]), .B(A[3]), .Ci(somador_completo_abstraido_3_co), .Soma(Saida[3]), .Co(Carry_Out));
  and and_1 (and_1_out, ~B[3], ~A[3], Saida[3]);  // AND_Gate
  and and_2 (and_2_out, B[3], A[3], ~Saida[3]);  // AND_Gate
  xor xor_1 (Overflow_2, somador_completo_abstraido_3_co, Carry_Out);
  or or_1 (Overflow, and_1_out, and_2_out);

  // Other names for the same wires on the sheet: _3 = B[3]
endmodule

module Mux_1_Bit (
  input  X,
  input  S,
  output S_2
);

  xor xor_1 (S_2, X, S);
endmodule
