// Logisim project overflow.circ as structural Verilog: 1 circuit, main circuit main
module main (
  input  bit_sinal,
  input  bit_sinal_2,
  input  _0,
  input  porta_posicao_3,
  input  _1,
  input  porta_posicao_3_2,
  input  _2,
  input  _3
);

  wire and_1_out, and_3_out, xor_1_out;

  and and_1 (and_1_out, _3, _3);
  // AND_Gate and_2 has open pins: in0=and_1_out, in1=xor_1_out, out=open
  // XOR_Gate xor_1 has open pins: out=xor_1_out
  and and_3 (and_3_out, ~bit_sinal, ~bit_sinal_2, porta_posicao_3, porta_posicao_3_2);  // AND_Gate

  // Notes on the sheet:
  //   recebe os bits de sinal
endmodule
