// Logisim project ULA.circ as structural Verilog: 17 circuits, main circuit CLA
module CLA (
  input  Ci,
  input  A,
  input  B,
  output Co
);

  wire G_out, P_2_out, P_out;

  and G (G_out, A, B);
  and P (P_out, A, Ci);
  and P_2 (P_2_out, Ci, B);
  or or_1 (Co, G_out, P_out, P_2_out);
endmodule

module Somador_de_4_Bits_CLA (
  input  [3:0] in_1,
  input  [3:0] in_2,
  output [3:0] out_3,
  output out_4
);

  Somador_Completo_CLA somador_completo_cla_1 ();  // open: An, Bn, Soma, Cin, Gn_1, G, Co
  Somador_Completo_CLA somador_completo_cla_2 ();  // open: An, Bn, Soma, Cin, Gn_1, G, Co
  Somador_Completo_CLA somador_completo_cla_3 ();  // open: An, Bn, Soma, Cin, Gn_1, G, Co
  Somador_Completo_CLA somador_completo_cla_4 ();  // open: An, Bn, Soma, Cin, Gn_1, G, Co

  // Other names for the same wires on the sheet: Output[3:0] = out_3; S0 = out_3[0]; S1 = out_3[1]; S2 = out_3[2];
  //   S3 = out_3[3]
endmodule

// Somador\nCLA
module Somador_Completo_CLA (
  input  Cin,
  input  An,
  input  Bn,
  input  Gn_1,
  output Soma,
  output G,
  output Co
);

  wire xor_2_out;

  CLA cla_1 (.Ci(Gn_1), .A(An), .B(Bn), .Co(Co));
  xor xor_1 (Soma, Cin, xor_2_out);
  xor xor_2 (xor_2_out, An, Bn);
endmodule

module Teste (
  input  [3:0] in_1,
  input  [3:0] in_2,
  input  in_3,
  output C0,
  output C1,
  output C1_2
);

  wire G0_out, G_2_out, G_out, P0_2_out, P0_out, P_2_out, P_3_out, P_4_out, P_out, undriven, undriven_2,
       undriven_3, undriven_4;

  and G0 (G0_out, in_2[0], in_1[0]);
  and P0 (P0_out, in_2[0], in_3);
  and P0_2 (P0_2_out, in_1[0], in_3);
  and G (G_out, in_2[1], in_1[1]);
  and P (P_out, in_2[1], G0_out);
  and P_2 (P_2_out, in_1[1], G0_out);
  // AND_Gate P0_3 is placed but not wired
  // AND_Gate P0_4 is placed but not wired
  // AND_Gate P1 is placed but not wired
  // AND_Gate P1_2 is placed but not wired
  and G_2 (G_2_out, undriven, undriven_2);
  and P_3 (P_3_out, undriven_3, G_out);
  and P_4 (P_4_out, undriven_4, G_out);
  or or_1 (C0, G0_out, P0_out, P0_2_out);
  or or_2 (C1, G_out, P_out, P_2_out);
  or or_3 (C1_2, G_2_out, P_3_out, P_4_out);
endmodule

module Somador_de_4_bits_completo (
  input  in_1,
  input  [3:0] A,
  input  [3:0] B,
  output [3:0] out_4
);

  wire somador_de_4_bits_1_overflow;
  wire [2:0] decodificador_display_1_s4, decodificador_display_2_s4, decodificador_display_3_s4;
  wire [3:0] decodificador_display_1_s0, decodificador_display_2_s0, decodificador_display_3_s0;

  LED Overflow (.in(somador_de_4_bits_1_overflow));
  Decodificador_Display decodificador_display_1 (
    .in_1(A), .S0(decodificador_display_1_s0[0]), .S1(decodificador_display_1_s0[1]),
    .S2(decodificador_display_1_s0[2]), .S3(decodificador_display_1_s0[3]),
    .S4(decodificador_display_1_s4[0]), .S5(decodificador_display_1_s4[1]), .S6(decodificador_display_1_s4[2]));
  Somador_De_4_Bits somador_de_4_bits_1 (
    .B(B), .A(A), .Saida(out_4), .B_Inverte(in_1), .Overflow(somador_de_4_bits_1_overflow));  // open: Carry_Out
  Decodificador_Display decodificador_display_2 (
    .in_1(B), .S0(decodificador_display_2_s0[0]), .S1(decodificador_display_2_s0[1]),
    .S2(decodificador_display_2_s0[2]), .S3(decodificador_display_2_s0[3]),
    .S4(decodificador_display_2_s4[0]), .S5(decodificador_display_2_s4[1]), .S6(decodificador_display_2_s4[2]));
  _7_Segment_Display u_7_segment_display_1 (
    .g(decodificador_display_1_s0[0]), .f(decodificador_display_1_s0[1]), .a(decodificador_display_1_s0[2]),
    .b(decodificador_display_1_s0[3]), .e(decodificador_display_1_s4[0]), .d(decodificador_display_1_s4[1]),
    .c(decodificador_display_1_s4[2]));  // open: dp
  _7_Segment_Display u_7_segment_display_2 (
    .g(decodificador_display_2_s0[0]), .f(decodificador_display_2_s0[1]), .a(decodificador_display_2_s0[2]),
    .b(decodificador_display_2_s0[3]), .e(decodificador_display_2_s4[0]), .d(decodificador_display_2_s4[1]),
    .c(decodificador_display_2_s4[2]));  // open: dp
  Decodificador_Display decodificador_display_3 (
    .in_1(out_4), .S0(decodificador_display_3_s0[0]), .S1(decodificador_display_3_s0[1]),
    .S2(decodificador_display_3_s0[2]), .S3(decodificador_display_3_s0[3]),
    .S4(decodificador_display_3_s4[0]), .S5(decodificador_display_3_s4[1]), .S6(decodificador_display_3_s4[2]));
  _7_Segment_Display u_7_segment_display_3 (
    .g(decodificador_display_3_s0[0]), .f(decodificador_display_3_s0[1]), .a(decodificador_display_3_s0[2]),
    .b(decodificador_display_3_s0[3]), .e(decodificador_display_3_s4[0]), .d(decodificador_display_3_s4[1]),
    .c(decodificador_display_3_s4[2]));  // open: dp
endmodule

module Somador_De_4_Bits (
  input  [3:0] A,
  input  B_Inverte,
  input  [3:0] B,
  output [3:0] Saida,
  output Overflow,
  output Carry_Out
);

  wire somador_completo_b_inverte_1_carry_out, somador_completo_b_inverte_2_carry_out,
       somador_completo_b_inverte_3_carry_out;

  Somador_Completo_B_Inverte somador_completo_b_inverte_1 (
    .Carry_Out(somador_completo_b_inverte_1_carry_out), .Soma(Saida[0]), .Ci(B_Inverte), .A(A[0]), .B(B[0]),
    .B_Inverte(B_Inverte));
  Somador_Completo_B_Inverte somador_completo_b_inverte_2 (
    .Carry_Out(somador_completo_b_inverte_2_carry_out), .Soma(Saida[1]),
    .Ci(somador_completo_b_inverte_1_carry_out), .A(A[1]), .B(B[1]), .B_Inverte(B_Inverte));
  Somador_Completo_B_Inverte somador_completo_b_inverte_3 (
    .Carry_Out(somador_completo_b_inverte_3_carry_out), .Soma(Saida[2]),
    .Ci(somador_completo_b_inverte_2_carry_out), .A(A[2]), .B(B[2]), .B_Inverte(B_Inverte));
  Somador_Completo_B_Inverte somador_completo_b_inverte_4 (
    .Carry_Out(Carry_Out), .Soma(Saida[3]), .Ci(somador_completo_b_inverte_3_carry_out), .A(A[3]), .B(B[3]),
    .B_Inverte(B_Inverte));
  xor xor_1 (Overflow, somador_completo_b_inverte_3_carry_out, Carry_Out);
endmodule

// Decoder
module Decodificador_Display (
  input  [3:0] in_1,
  output S0,
  output S1,
  output S2,
  output S3,
  output S4,
  output S5,
  output S6
);

  wire and_1_out, and_2_out, and_3_out, and_4_out, and_5_out, and_6_out, and_7_out, and_8_out, and_9_out,
       and_10_out, and_11_out, and_12_out, and_13_out, and_14_out, and_15_out, and_16_out, and_17_out,
       and_18_out, and_19_out, and_20_out, and_21_out, and_22_out, and_23_out, and_24_out, and_25_out,
       and_26_out, and_27_out, and_28_out, and_29_out, and_30_out, and_31_out, and_32_out, and_33_out,
       and_34_out, and_35_out, not_1_out, not_2_out, not_3_out, not_4_out, not_5_out, not_6_out, not_7_out,
       not_8_out, not_9_out, not_10_out, not_11_out, not_12_out, not_13_out, not_14_out, not_15_out,
       not_16_out, not_17_out, not_18_out, not_19_out, not_20_out, not_21_out, not_22_out, not_23_out,
       not_24_out, not_25_out, not_26_out, not_27_out, not_28_out, not_29_out, not_30_out, not_31_out,
       not_32_out, not_33_out, not_34_out, not_35_out, not_36_out, not_37_out, not_38_out, not_39_out,
       not_40_out, not_41_out, not_42_out, not_43_out;

  not not_1 (not_1_out, in_1[2]);
  not not_2 (not_2_out, in_1[0]);
  not not_3 (not_3_out, in_1[3]);
  not not_4 (not_4_out, in_1[1]);
  not not_5 (not_5_out, in_1[2]);
  not not_6 (not_6_out, in_1[1]);
  not not_7 (not_7_out, in_1[0]);
  not not_8 (not_8_out, in_1[3]);
  not not_9 (not_9_out, in_1[1]);
  not not_10 (not_10_out, in_1[0]);
  not not_11 (not_11_out, in_1[2]);
  not not_12 (not_12_out, in_1[2]);
  not not_13 (not_13_out, in_1[0]);
  not not_14 (not_14_out, in_1[3]);
  not not_15 (not_15_out, in_1[3]);
  not not_16 (not_16_out, in_1[2]);
  not not_17 (not_17_out, in_1[1]);
  not not_18 (not_18_out, in_1[0]);
  not not_19 (not_19_out, in_1[3]);
  not not_20 (not_20_out, in_1[2]);
  not not_21 (not_21_out, in_1[3]);
  not not_22 (not_22_out, in_1[1]);
  not not_23 (not_23_out, in_1[0]);
  not not_24 (not_24_out, in_1[2]);
  not not_25 (not_25_out, in_1[0]);
  not not_26 (not_26_out, in_1[3]);
  not not_27 (not_27_out, in_1[1]);
  not not_28 (not_28_out, in_1[2]);
  not not_29 (not_29_out, in_1[0]);
  not not_30 (not_30_out, in_1[0]);
  not not_31 (not_31_out, in_1[3]);
  not not_32 (not_32_out, in_1[2]);
  not not_33 (not_33_out, in_1[0]);
  not not_34 (not_34_out, in_1[2]);
  not not_35 (not_35_out, in_1[1]);
  not not_36 (not_36_out, in_1[0]);
  not not_37 (not_37_out, in_1[1]);
  not not_38 (not_38_out, in_1[3]);
  not not_39 (not_39_out, in_1[1]);
  not not_40 (not_40_out, in_1[3]);
  not not_41 (not_41_out, in_1[1]);
  not not_42 (not_42_out, in_1[3]);
  not not_43 (not_43_out, in_1[2]);
  and and_1 (and_1_out, not_1_out, in_1[1]);
  and and_2 (and_2_out, in_1[1], not_2_out);
  and and_3 (and_3_out, not_3_out, in_1[2], not_4_out);
  and and_4 (and_4_out, in_1[3], not_5_out);
  and and_5 (and_5_out, in_1[3], in_1[0]);
  and and_6 (and_6_out, not_6_out, not_7_out);
  and and_7 (and_7_out, not_8_out, in_1[2], not_9_out);
  and and_8 (and_8_out, in_1[2], not_10_out);
  and and_9 (and_9_out, in_1[3], not_11_out);
  and and_10 (and_10_out, in_1[3], in_1[1]);
  and and_11 (and_11_out, not_12_out, not_13_out);
  and and_12 (and_12_out, not_14_out, in_1[1]);
  and and_13 (and_13_out, not_15_out, in_1[2], in_1[0]);
  and and_14 (and_14_out, in_1[2], in_1[1]);
  and and_15 (and_15_out, in_1[3], not_16_out, not_17_out);
  and and_16 (and_16_out, in_1[3], not_18_out);
  and and_17 (and_17_out, not_19_out, not_20_out);
  and and_18 (and_18_out, not_21_out, not_22_out, not_23_out);
  and and_19 (and_19_out, not_24_out, not_25_out);
  and and_20 (and_20_out, not_26_out, in_1[1], in_1[0]);
  and and_21 (and_21_out, in_1[3], not_27_out, in_1[0]);
  and and_22 (and_22_out, not_28_out, not_29_out);
  and and_23 (and_23_out, in_1[1], not_30_out);
  and and_24 (and_24_out, in_1[3], in_1[1]);
  and and_25 (and_25_out, in_1[3], in_1[2]);
  and and_26 (and_26_out, not_31_out, not_32_out, not_33_out);
  and and_27 (and_27_out, not_34_out, in_1[1], in_1[0]);
  and and_28 (and_28_out, in_1[2], not_35_out, in_1[0]);
  and and_29 (and_29_out, in_1[2], in_1[1], not_36_out);
  and and_30 (and_30_out, in_1[3], not_37_out);
  and and_31 (and_31_out, not_38_out, not_39_out);
  and and_32 (and_32_out, not_40_out, in_1[0]);
  and and_33 (and_33_out, not_41_out, in_1[0]);
  and and_34 (and_34_out, not_42_out, in_1[2]);
  and and_35 (and_35_out, in_1[3], not_43_out);
  or or_1 (S0, and_1_out, and_2_out, and_3_out, and_4_out, and_5_out);
  or or_2 (S1, and_6_out, and_7_out, and_8_out, and_9_out, and_10_out);
  or or_3 (S2, and_11_out, and_12_out, and_13_out, and_14_out, and_15_out, and_16_out);
  or or_4 (S3, and_17_out, and_18_out, and_19_out, and_20_out, and_21_out);
  or or_5 (S4, and_22_out, and_23_out, and_24_out, and_25_out);
  or or_6 (S5, and_26_out, and_27_out, and_28_out, and_29_out, and_30_out);
  or or_7 (S6, and_31_out, and_32_out, and_33_out, and_34_out, and_35_out);
endmodule

// ULA
module ULA_de_1_Bit___Op__Code_2_Bits (
  input  B_Inverte,
  input  Carry_In,
  input  [1:0] in_3,
  input  A,
  input  B,
  output S,
  output Carry_Out
);

  wire and_1_out, mux_duas_entradas_1_s_2, not_1_out, not_2_out, or_1_out, somador_completo_1_soma;

  Mux_Duas_Entradas mux_duas_entradas_1 (.S_2(mux_duas_entradas_1_s_2), .A(B), .B(not_1_out), .S(B_Inverte));
  not not_1 (not_1_out, B);
  Somador_Completo somador_completo_1 (
    .Soma(somador_completo_1_soma), .Ci(Carry_In), .A(A), .B(mux_duas_entradas_1_s_2), .out_5(Carry_Out));
  and and_1 (and_1_out, A, mux_duas_entradas_1_s_2);
  or or_1 (or_1_out, A, mux_duas_entradas_1_s_2);
  not not_2 (not_2_out, A);
  Multiplexador___Op__Code_de_2_Bits multiplexador_op_code_de_2_bits_1 (
    .out_6(S), ._3(somador_completo_1_soma), ._2(not_2_out), ._1(or_1_out), ._0(and_1_out), .in_1(in_3));
endmodule

module Mux_1_Bit (
  input  X,
  input  S,
  output S_2
);

  xor xor_1 (S_2, X, S);
endmodule

// Mux
module Mux_Duas_Entradas (
  input  A,
  input  B,
  input  S,
  output S_2
);

  wire and_1_out, and_2_out;

  and and_1 (and_1_out, ~S, A);  // AND_Gate
  or or_1 (S_2, and_1_out, and_2_out);
  and and_2 (and_2_out, S, B);
endmodule

// Multiplexador
module Multiplexador___Op__Code_de_2_Bits (
  input  [1:0] in_1,
  input  _0,
  input  _1,
  input  _2,
  input  _3,
  output out_6
);

  wire _0_out, _1_out, _2_out, _3_out;

  and u__0 (_0_out, _0, ~in_1[0], ~in_1[1]);  // AND_Gate
  and u__1 (_1_out, _1, in_1[0], ~in_1[1]);  // AND_Gate
  and u__2 (_2_out, _2, ~in_1[0], in_1[1]);  // AND_Gate
  and u__3 (_3_out, _3, in_1[0], in_1[1]);
  or or_1 (out_6, _0_out, _1_out, _2_out, _3_out);
endmodule

module ULA_de_4_bits___Op__Code_2_bits (
  input  [3:0] A,
  input  [3:0] B,
  input  B_Inverte,
  input  [1:0] Op__Code,
  output [3:0] out_5,
  output out_6
);

  wire ula_de_1_bit_op_code_2_bits_1_carry_out, ula_de_1_bit_op_code_2_bits_2_carry_out,
       ula_de_1_bit_op_code_2_bits_3_carry_out;

  ULA_de_1_Bit___Op__Code_2_Bits ula_de_1_bit_op_code_2_bits_1 (
    .A(A[0]), .B(B[0]), .B_Inverte(B_Inverte), .Carry_In(B_Inverte), .in_3(Op__Code),
    .Carry_Out(ula_de_1_bit_op_code_2_bits_1_carry_out), .S(out_5[0]));
  ULA_de_1_Bit___Op__Code_2_Bits ula_de_1_bit_op_code_2_bits_2 (
    .A(A[1]), .B(B[1]), .B_Inverte(B_Inverte), .Carry_In(ula_de_1_bit_op_code_2_bits_1_carry_out),
    .in_3(Op__Code), .Carry_Out(ula_de_1_bit_op_code_2_bits_2_carry_out), .S(out_5[1]));
  ULA_de_1_Bit___Op__Code_2_Bits ula_de_1_bit_op_code_2_bits_3 (
    .A(A[2]), .B(B[2]), .B_Inverte(B_Inverte), .Carry_In(ula_de_1_bit_op_code_2_bits_2_carry_out),
    .in_3(Op__Code), .Carry_Out(ula_de_1_bit_op_code_2_bits_3_carry_out), .S(out_5[2]));
  ULA_de_1_Bit___Op__Code_2_Bits ula_de_1_bit_op_code_2_bits_4 (
    .A(A[3]), .B(B[3]), .B_Inverte(B_Inverte), .Carry_In(ula_de_1_bit_op_code_2_bits_3_carry_out),
    .in_3(Op__Code), .Carry_Out(out_6), .S(out_5[3]));
endmodule

module ULA_de_4_Bits___Op__Code_4_Bits (
  input  [3:0] A,
  input  [3:0] B,
  input  [3:0] Op__Code,
  output [3:0] out_4
);

  wire [3:0] _0, _1, _2, _4, _5, _6, _7, _8, _9, B_t, D, E;

  assign _0 = ~A;  // NOT_Gate not_1, 4 bits wide
  assign _2 = ~A & B;  // AND_Gate and_1, 4 bits wide
  assign _1 = ~(A | B);  // NOR_Gate nor_1, 4 bits wide
  assign _5 = ~B;  // NOT_Gate not_2, 4 bits wide
  assign _4 = ~(A & B);  // NAND_Gate nand_1, 4 bits wide
  assign _7 = A & ~B;  // AND_Gate and_2, 4 bits wide
  assign _6 = A ^ B;  // XOR_Gate xor_1, 4 bits wide
  assign _8 = ~A | B;  // OR_Gate or_1, 4 bits wide
  Multiplexer #(.select(4), .width(4), .enable("false")) multiplexer_1 (
    .in0(_0), .in1(_1), .in2(_2), .in3(4'b0000), .in4(_4), .in5(_5), .in6(_6), .in7(_7), .in8(_8), .in9(_9),
    .in10(B), .in11(B_t), .in12(4'b1111), .in13(D), .in14(E), .in15(A), .out(out_4), .sel(Op__Code));
  assign _9 = ~(A ^ B);  // XNOR_Gate xnor_1, 4 bits wide
  assign B_t = A & B;  // AND_Gate and_3, 4 bits wide
  assign D = A | ~B;  // OR_Gate or_2, 4 bits wide
  assign E = A | B;  // OR_Gate or_3, 4 bits wide

  // Other names for the same wires on the sheet: A_t[3:0] = B; F[3:0] = A
endmodule

module Somador_Completo__Abstraido (
  input  A,
  input  B,
  input  Ci,
  output Soma,
  output Co
);

  wire meio_somador_1_carry_out, meio_somador_1_soma, meio_somador_2_carry_out;

  Meio_Somador meio_somador_1 (.Soma(meio_somador_1_soma), .Carry_Out(meio_somador_1_carry_out), .A0(A), .B0(B));
  Meio_Somador meio_somador_2 (.Soma(Soma), .Carry_Out(meio_somador_2_carry_out), .A0(meio_somador_1_soma), .B0(Ci));
  or or_1 (Co, meio_somador_2_carry_out, meio_somador_1_carry_out);
endmodule

// Somador\n Completo
module Somador_Completo_B_Inverte (
  input  Ci,
  input  A,
  input  B,
  input  B_Inverte,
  output Carry_Out,
  output Soma
);

  wire and_1_out, and_2_out, mux_1_bit_1_s_2, xor_1_out;

  Mux_1_Bit mux_1_bit_1 (.X(B), .S(B_Inverte), .S_2(mux_1_bit_1_s_2));
  xor xor_1 (xor_1_out, A, mux_1_bit_1_s_2);
  and and_1 (and_1_out, A, mux_1_bit_1_s_2);
  xor xor_2 (Soma, Ci, xor_1_out);
  and and_2 (and_2_out, Ci, xor_1_out);
  or or_1 (Carry_Out, and_1_out, and_2_out);
endmodule

// Somador
module Somador_Completo (
  input  Ci,
  input  A,
  input  B,
  output Soma,
  output out_5
);

  wire and_1_out, and_2_out, xor_1_out;

  and and_1 (and_1_out, B, A);
  xor xor_1 (xor_1_out, A, B);
  or or_1 (out_5, and_1_out, and_2_out);
  and and_2 (and_2_out, xor_1_out, Ci);
  xor xor_2 (Soma, Ci, xor_1_out);
endmodule

// Meio\nSomador
module Meio_Somador (
  input  A0,
  input  B0,
  output Soma,
  output Carry_Out
);

  xor xor_1 (Soma, A0, B0);
  and and_1 (Carry_Out, A0, B0);
endmodule
