// Logisim project ComparadorDeMagnitude2Bits.circ as structural Verilog: 1 circuit, main circuit main
module main (
  input  [1:0] A,
  input  [1:0] B,
  output out_3,
  output out_4,
  output out_5
);

  wire not_1_out, not_2_out;

  not not_1 (not_1_out, B[0]);
  not not_2 (not_2_out, B[1]);
  and and_1 (out_3, A[0], not_1_out);
  and and_2 (out_5, A[1], not_2_out);
  or or_1 (out_4, out_3, out_5);

  // Notes on the sheet:
  //   Circuito Comparador Completo de 2 Bits
  //   (A0'B0) + (A1'B1)
endmodule
