// Logisim project ComparadorDeMagnitude3Bits.circ as structural Verilog: 1 circuit, main circuit main
module main (
  input  [2:0] A,
  input  [2:0] B,
  output out_3
);

  wire and_1_out, and_2_out, and_3_out, and_4_out, and_5_out, and_6_out, and_7_out, not_1_out, not_2_out,
       not_3_out, not_4_out, not_5_out, not_6_out, not_7_out, not_8_out, not_9_out, not_10_out, not_11_out,
       not_12_out;

  not not_1 (not_1_out, B[0]);
  not not_2 (not_2_out, B[0]);
  not not_3 (not_3_out, B[1]);
  not not_4 (not_4_out, B[1]);
  not not_5 (not_5_out, B[0]);
  not not_6 (not_6_out, B[1]);
  not not_7 (not_7_out, B[2]);
  not not_8 (not_8_out, B[0]);
  not not_9 (not_9_out, B[2]);
  not not_10 (not_10_out, B[1]);
  not not_11 (not_11_out, B[2]);
  not not_12 (not_12_out, B[2]);
  and and_1 (and_1_out, A[0], not_1_out);
  and and_2 (and_2_out, A[1], not_2_out, not_3_out);
  and and_3 (and_3_out, A[0], A[1], not_4_out);
  and and_4 (and_4_out, A[2], not_5_out, not_6_out, not_7_out);
  and and_5 (and_5_out, A[1], A[2], not_8_out, not_9_out);
  and and_6 (and_6_out, A[0], A[2], not_10_out, not_11_out);
  and and_7 (and_7_out, A[0], A[1], A[2], not_12_out);
  or or_1 (out_3, and_1_out, and_2_out, and_3_out, and_4_out, and_5_out, and_6_out, and_7_out);

  // Notes on the sheet:
  //   Circuito Comparador Completo de 3 Bits
endmodule
