// Logisim project ComparadorDeMagnitudeUmBit.circ as structural Verilog: 1 circuit, main circuit main
module main (
  input  A,
  input  B,
  output out_3
);

  wire not_1_out;

  not not_1 (not_1_out, B);
  and and_1 (out_3, A, not_1_out);

  // Notes on the sheet:
  //   Circuito Comparador de Magnitude de Um Bit
endmodule
