// Logisim project Mux4x1Completo.circ as structural Verilog: 1 circuit, main circuit main
module main (
  input  [3:0] _3_2_1_0,
  input  [1:0] in_2,
  output [3:0] _3_2_1_0_2
);

  wire _0_out, _1_out, _2_out, _3_out, not_1_out, not_2_out, not_3_out, not_4_out;

  and _3 (_3_out, in_2[1], in_2[0]);
  and AND (_3_2_1_0_2[3], _3_2_1_0[3], _3_out);
  and AND_2 (_3_2_1_0_2[2], _3_2_1_0[2], _2_out);
  and AND_3 (_3_2_1_0_2[1], _3_2_1_0[1], _1_out);
  and AND_4 (_3_2_1_0_2[0], _3_2_1_0[0], _0_out);
  and _1 (_1_out, not_3_out, in_2[0]);
  and _2 (_2_out, in_2[1], not_4_out);
  and _0 (_0_out, not_2_out, not_1_out);
  not not_1 (not_1_out, in_2[0]);
  not not_2 (not_2_out, in_2[1]);
  not not_3 (not_3_out, in_2[1]);
  not not_4 (not_4_out, in_2[0]);

  // Notes on the sheet:
  //   Multiplexador 4x1 Completo
endmodule
