// Logisim project Mux4x1Simplificado.circ as structural Verilog: 1 circuit, main circuit main
module main (
  input  [3:0] _3_2_1_0,
  input  [1:0] _1_0,
  output [3:0] _3_2_1_0_2
);

  wire not_1_out, not_2_out, not_3_out, not_4_out;

  and AND (_3_2_1_0_2[3], _3_2_1_0[3], _1_0[0], _1_0[1]);
  and AND_2 (_3_2_1_0_2[2], _3_2_1_0[2], not_1_out, _1_0[1]);
  not not_1 (not_1_out, _1_0[0]);
  and AND_3 (_3_2_1_0_2[1], _3_2_1_0[1], _1_0[0], not_2_out);
  not not_2 (not_2_out, _1_0[1]);
  not not_3 (not_3_out, _1_0[0]);
  and AND_4 (_3_2_1_0_2[0], _3_2_1_0[0], not_3_out, not_4_out);
  not not_4 (not_4_out, _1_0[1]);

  // Notes on the sheet:
  //   Multiplexador 4x1 Simplificado
endmodule
