// Logisim project Latch_SR_Controlado_(Nand).circ as structural Verilog: 2 circuits, main circuit Latch SR Controlado (Nand)
module Latch_SR_Controlado__Nand (
  input  S,
  input  En,
  input  R,
  output out_4,
  output out_5
);

  wire nand_1_out, nand_2_out;

  nand nand_1 (nand_1_out, S, En);
  nand nand_2 (nand_2_out, En, R);
  Latch_SR__Nand latch_sr_nand_1 (.Q_prime(out_5), .Q(out_4), .S(nand_1_out), .R(nand_2_out));
endmodule

module Latch_SR__Nand (
  input  S,
  input  R,
  output Q,
  output Q_prime
);

  nand nand_1 (Q, S, Q_prime);
  nand nand_2 (Q_prime, Q, R);
endmodule
