// Logisim project SomadorCompleto4Bits.circ as structural Verilog: 1 circuit, main circuit main
module main (
  input  [3:0] A,
  input  [3:0] B,
  input  Ci,
  output [4:0] Soma
);

  wire AND_2_out, AND_3_out, AND_4_out, AND_5_out, AND_6_out, AND_7_out, AND_8_out, AND_9_out, AND_10_out,
       AND_11_out, AND_12_out, AND_out, OR_2_out, OR_3_out, OR_4_out, XOR_3_out, XOR_5_out, XOR_7_out,
       XOR_out;

  xor XOR (XOR_out, A[3], B[3]);
  and AND (AND_out, A[3], B[3]);
  and AND_2 (AND_2_out, A[3], OR_2_out);
  or OR (Soma[4], AND_out, AND_2_out, AND_3_out);
  and AND_3 (AND_3_out, B[3], OR_2_out);
  xor XOR_2 (Soma[3], XOR_out, OR_2_out);
  and AND_4 (AND_4_out, A[2], B[2]);
  or OR_2 (OR_2_out, AND_4_out, AND_5_out, AND_6_out);
  and AND_5 (AND_5_out, A[2], OR_3_out);
  and AND_6 (AND_6_out, B[2], OR_3_out);
  xor XOR_3 (XOR_3_out, A[2], B[2]);
  xor XOR_4 (Soma[2], XOR_3_out, OR_3_out);
  and AND_7 (AND_7_out, A[1], B[1]);
  and AND_8 (AND_8_out, A[1], OR_4_out);
  and AND_9 (AND_9_out, B[1], OR_4_out);
  xor XOR_5 (XOR_5_out, A[1], B[1]);
  or OR_3 (OR_3_out, AND_7_out, AND_8_out, AND_9_out);
  xor XOR_6 (Soma[1], XOR_5_out, OR_4_out);
  and AND_10 (AND_10_out, A[0], B[0]);
  and AND_11 (AND_11_out, A[0], Ci);
  and AND_12 (AND_12_out, B[0], Ci);
  xor XOR_7 (XOR_7_out, A[0], B[0]);
  or OR_4 (OR_4_out, AND_10_out, AND_11_out, AND_12_out);
  xor XOR_8 (Soma[0], XOR_7_out, Ci);

  // Notes on the sheet:
  //   Circuito Somador Completo de 4 bits
endmodule
